# Fritzing sketch 20180130 (saved by Fritzing 0.9.3b)
breadboards: 1

parts:
  パーツ1 = Arduino Uno (Rev3)
  S1 = Pushbutton [package="[THT]"]
  LED1 = LED - 5mm [color="Red (633nm)" package="5 mm [THT]"]
  S2 = Round Pushbutton

nets:
  N1: パーツ1.D13/SCK, LED1.anode
  N2: パーツ1.D6_PWM, パーツ1.D7, パーツ1.3V3, S1.Pin_3, S1.Pin_4, S2.leg0
  N3: パーツ1.GND, S1.Pin_1, S1.Pin_2, LED1.cathode, S2.leg1
