# Fritzing sketch 20180201 (saved by Fritzing 0.9.3b)
breadboards: 1

parts:
  パーツ1 = Arduino Uno (Rev3)
  LED1 = LED - 5mm [color="Red (633nm)" package="5 mm [THT]"]
  S1 = Round Pushbutton
  S2 = Round Pushbutton
  S3 = Round Pushbutton
  S4 = Round Pushbutton
  S5 = Pushbutton [package="[THT]"]

nets:
  N1: パーツ1.D13/SCK, LED1.anode
  N2: パーツ1.D3_PWM, パーツ1.D4, パーツ1.D5_PWM, パーツ1.D6_PWM, パーツ1.D7, パーツ1.3V3, S1.leg0, S2.leg0, S3.leg0, S4.leg0, S5.Pin_1, S5.Pin_2
  N3: パーツ1.GND, LED1.cathode, S1.leg1, S2.leg1, S3.leg1, S4.leg1, S5.Pin_3, S5.Pin_4

notes:
  PINK
  BLUE
  YELLOW
  GREEN
